# Fritzing sketch sys_auth (saved by Fritzing 0.9.3b)
breadboards: 1

parts:
  LCD1 = LCD screen
  LCM1602_IIC1 = LCM1602 IIC [part_number="LCM1602 IIC" chip_label="LCM1602 IIC" package="DIP (Dual Inline) [THT]"]
  Composant1 = Arduino Uno (Rev3)
  LED1 = LED - 5mm [color="Red (633nm)" package="5 mm [THT]"]  # not connected
  LED2 = LED - 5mm [color="Green (555nm)" package="5 mm [THT]"]  # not connected
  R1 = Resistor [tolerance=±5% resistance=220 package=THT]
  R2 = Resistor [tolerance=±5% resistance=220 package=THT]
  Matrix_keypad1 = KEYPAD 4x4

nets:
  VSS: LCD1.VSS, LCM1602_IIC1.VSS
  VDD: LCD1.VDD, LCM1602_IIC1.VDD
  N1: LCD1.V0, LCM1602_IIC1.V0
  N2: LCD1.RS, LCM1602_IIC1.RS
  N3: LCD1.R/W, LCM1602_IIC1.RW
  N4: LCD1.E, LCM1602_IIC1.E
  N5: LCD1.DB0, LCM1602_IIC1.D0
  N6: LCD1.DB1, LCM1602_IIC1.D1
  N7: LCD1.DB2, LCM1602_IIC1.D2
  N8: LCD1.DB3, LCM1602_IIC1.D3
  N9: LCD1.DB4, LCM1602_IIC1.D4
  N10: LCD1.DB5, LCM1602_IIC1.D5
  N11: LCD1.DB6, LCM1602_IIC1.D6
  N12: LCD1.DB7, LCM1602_IIC1.D7
  N13: LCD1.LED+, LCM1602_IIC1.A
  N14: LCD1.LED-, LCM1602_IIC1.K
  GND: LCM1602_IIC1.GND, Composant1.GND
  VCC: LCM1602_IIC1.VCC, Composant1.5V
  N15: LCM1602_IIC1.SDA, Composant1.A5/SCL
  N16: LCM1602_IIC1.SCL, Composant1.A4/SDA
  N17: Composant1.D8, Matrix_keypad1.row3
  N18: Composant1.D9_PWM, Matrix_keypad1.row4
  N19: Composant1.D12/MISO, R1.Pin_0
  N20: Composant1.D13/SCK, R2.Pin_0
  N21: Composant1.D2, Matrix_keypad1.col1
  N22: Composant1.D3_PWM, Matrix_keypad1.col2
  N23: Composant1.D4, Matrix_keypad1.col3
  N24: Composant1.D5_PWM, Matrix_keypad1.col4
  N25: Composant1.D6_PWM, Matrix_keypad1.row1
  N26: Composant1.D7, Matrix_keypad1.row2

custom parts:
  LCM1602 IIC: I2C-Module to use a 1602 or 2004 LCD on with the wire.h libory Serial LCD Modul
  KEYPAD 4x4: Matrix keypad 16 buttons, 4 rows x 4 columns
